# Fritzing sketch Breadboard (saved by Fritzing 0.9.3b)
breadboards: 1

parts:
  Temp_sensor = IC, DIP package, 8 pins [chip_label=TMP75]
  Body_Sensor = HC-SR501 Body Sensor Module
  Speaker = Piezo Speaker
  R2 = Resistor [tolerance=±5% resistance=5k package=THT]
  R3 = Resistor [tolerance=±5% resistance=5k package=THT]
  433MHz_Tx = FS1000A - 433Mhz RF Transmitter [package=THT]
  ANT1 = Antenna
  433MHz_Rx = XD-RF-5V [package=THT]
  ANT2 = Antenna
  Raspberry_Pi = Adafruit T-Cobbler Plus [part_number=T-connector]
  R4 = Resistor [tolerance=±5% resistance=5k package=THT]
  R5 = Resistor [tolerance=±5% resistance=5k package=THT]
  NodeMCU1 = NodeMCU V1.0
  Temp_sensor1 = IC, DIP package, 8 pins [chip_label=TMP75]
  Light_sensor1 = IC, SIP package, 4 pins [chip_label=VEML7700]

nets:
  N1: Temp_sensor.pin1, R3.Pin_1, Raspberry_Pi.SDA
  N2: Temp_sensor.pin2, R2.Pin_1, Raspberry_Pi.SCL
  GND: Temp_sensor.pin4, Temp_sensor.pin5, Temp_sensor.pin6, Temp_sensor.pin7, Body_Sensor.GND, Speaker.pin1, 433MHz_Tx.GND, 433MHz_Rx.GND, Raspberry_Pi.GND, NodeMCU1.GND, Temp_sensor1.pin4, Temp_sensor1.pin5, Temp_sensor1.pin6, Temp_sensor1.pin7, Light_sensor1.pin3
  3.3V: Temp_sensor.pin8, R2.Pin_0, R3.Pin_0, Raspberry_Pi.+3.3V, R4.Pin_0, R5.Pin_0, NodeMCU1.3V3, Temp_sensor1.pin8, Light_sensor1.pin2
  5V: Body_Sensor.VCC, 433MHz_Tx.VCC, 433MHz_Rx.VCC, Raspberry_Pi.+5V
  N3: Body_Sensor.OUT, Raspberry_Pi.GPIO18
  N4: Speaker.pin2, Raspberry_Pi.GPIO22
  N5: 433MHz_Tx.DATA, Raspberry_Pi.GPIO27
  N6: 433MHz_Tx.Antenna, ANT1.antenna_lead
  N7: 433MHz_Rx.DATA#2, Raspberry_Pi.GPIO17
  N8: 433MHz_Rx.Attenna, ANT2.antenna_lead
  N9: R4.Pin_1, NodeMCU1.D1, Temp_sensor1.pin2, Light_sensor1.pin1
  N10: R5.Pin_1, NodeMCU1.D2, Temp_sensor1.pin1, Light_sensor1.pin4

custom parts:
  HC-SR501 Body Sensor Module: Pyroelectric Infrared PIR Motion Sensor Detector Module
  FS1000A - 433Mhz RF Transmitter: This is 433Mhz RF transmitter with receiver kit for Arduino ARM MCU wireless Application environment: Remote control switch, receiver module, motorcycles, automobile anti-theft products, home security products, electric doors, shutter doors, windows, remote control socket, remote control LED, remote audio remote control electric doors, garage door remote control, remote control retractable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
  XD-RF-5V: This is 433Mhz RF transmitter with receiver kit for Arduino ARM MCU wireless Application environment: Remote control switch, receiver module, motorcycles, automobile anti-theft products, home security products, electric doors, shutter doors, windows, remote control socket, remote control LED, remote audio remote control electric doors, garage door remote control, remote control retractable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
  Adafruit T-Cobbler Plus: The Raspberry Pi has landed on the Maker World like a 40-GPIO pinned, quad-USB ported, credit card sized bomb of DIY joy. And while you can use most of our great Model B accessories by hooking up our downgrade cable, its probably a good time to upgrade your set up and accessorize using all of the 40 pins. That's why we now carry the Assembled Adafruit Pi T-Cobbler Plus - Breakout + Cable for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
  NodeMCU V1.0: ESP8266 based NodeMCU
