# Fritzing sketch NodeMcu (saved by Fritzing 0.9.3b)
circuit board: 2.6149cm x 4.07756cm

parts:
  NodeMCU = NodeMCU V1.0
  LED3 = LED - 5mm [color="Red (633nm)" package="5 mm [THT]"]
  Temp_sensor = IC, DIP package, 8 pins [chip_label=TMP75]
  Light_sensor = IC, SIP package, 4 pins [chip_label=VEML7700]
  LED4 = LED - 5mm [color="Green (555nm)" package="5 mm [THT]"]
  M1 = DC Motor  # not connected
  R1 = Resistor [tolerance=±5% resistance=47 package=THT]
  R3 = Resistor [tolerance=±5% resistance=5k package=THT]
  R2 = Resistor [tolerance=±5% resistance=5k package=THT]
  R4 = Resistor [tolerance=±5% resistance=47 package=THT]

nets:
  N1: NodeMCU.D1, Temp_sensor.pin2, Light_sensor.pin1, R2.Pin_1
  N2: NodeMCU.D2, Temp_sensor.pin1, Light_sensor.pin4, R3.Pin_1
  N3: NodeMCU.D3, LED3.anode
  N4: NodeMCU.D4, LED4.anode
  N5: NodeMCU.3V3, Temp_sensor.pin5, Temp_sensor.pin6, Temp_sensor.pin7, Temp_sensor.pin8, Light_sensor.pin2, R3.Pin_0, R2.Pin_0
  N6: NodeMCU.GND, Temp_sensor.pin4, Light_sensor.pin3, R1.Pin_1, R4.Pin_1
  N7: LED3.cathode, R1.Pin_0
  N8: LED4.cathode, R4.Pin_0

custom parts:
  NodeMCU V1.0: ESP8266 based NodeMCU
