# Fritzing sketch Raspberry (saved by Fritzing 0.9.3b)
circuit board: 6.23534cm x 3.00333cm

parts:
  Raspberry_Pi_3 = Raspberry Pi 3
  Temp_sensor = IC, DIP package, 8 pins [chip_label=TMP75]
  Body_Sensor = HC-SR501 Body Sensor Module
  LED3 = LED - 5mm [color="Green (555nm)" package="5 mm [THT]"]
  Speaker = Piezo Speaker
  J4 = female pin header, 3 pins [form="♀ (female)"]
  J7 = male pin header, 3 pins [form="♂ (male)"]
  R1 = Resistor [tolerance=±5% resistance=47 package=THT]
  R2 = Resistor [tolerance=±5% resistance=5k package=THT]
  R3 = Resistor [tolerance=±5% resistance=5k package=THT]
  433MHz_Tx = FS1000A - 433Mhz RF Transmitter [package=THT]
  J8 = female pin header, 3 pins [form="♀ (female)"]
  ANT1 = Antenna
  433MHz_Rx = XD-RF-5V [package=THT]
  J9 = female pin header, 4 pins [form="♀ (female)"]
  ANT2 = Antenna

nets:
  3V3: Raspberry_Pi_3.3v3, Raspberry_Pi_3.3V3, Temp_sensor.pin8, R2.Pin_0, R3.Pin_0
  N1: Raspberry_Pi_3.GPIO2, Temp_sensor.pin1, R3.Pin_1
  N2: Raspberry_Pi_3.GPIO3, Temp_sensor.pin2, R2.Pin_1
  N3: Raspberry_Pi_3.GPIO4, R1.Pin_1
  GND: Raspberry_Pi_3.GND, Temp_sensor.pin4, Temp_sensor.pin5, Temp_sensor.pin6, Temp_sensor.pin7, LED3.cathode, Speaker.pin1, J7.pin1, 433MHz_Tx.GND, J8.pin3, 433MHz_Rx.GND, J9.pin4
  N4: Raspberry_Pi_3.GPIO17, 433MHz_Rx.DATA, J9.pin2
  N5: Raspberry_Pi_3.GPIO27, 433MHz_Tx.DATA, J8.pin1
  N6: Raspberry_Pi_3.GPIO22, Speaker.pin2
  N7: Raspberry_Pi_3.GPIO18, J7.pin2
  VCC: Raspberry_Pi_3.5V, J7.pin3, 433MHz_Tx.VCC, J8.pin2, 433MHz_Rx.VCC, J9.pin1
  N8: Body_Sensor.VCC, J4.pin3
  N9: Body_Sensor.OUT, J4.pin2
  N10: Body_Sensor.GND, J4.pin1
  N11: LED3.anode, R1.Pin_0
  N12: 433MHz_Tx.Antenna, ANT1.antenna_lead
  N13: 433MHz_Rx.Attenna, ANT2.antenna_lead

custom parts:
  HC-SR501 Body Sensor Module: Pyroelectric Infrared PIR Motion Sensor Detector Module
  FS1000A - 433Mhz RF Transmitter: This is 433Mhz RF transmitter with receiver kit for Arduino ARM MCU wireless Application environment: Remote control switch, receiver module, motorcycles, automobile anti-theft products, home security products, electric doors, shutter doors, windows, remote control socket, remote control LED, remote audio remote control electric doors, garage door remote control, remote control retractable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
  XD-RF-5V: This is 433Mhz RF transmitter with receiver kit for Arduino ARM MCU wireless Application environment: Remote control switch, receiver module, motorcycles, automobile anti-theft products, home security products, electric doors, shutter doors, windows, remote control socket, remote control LED, remote audio remote control electric doors, garage door remote control, remote control retractable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
